// Logisim project real_alu.circ as structural Verilog
module main (
);


  // Notes on the sheet:
  //   REAL_ALU
endmodule

module inA_inB (
  input  [7:0] inA,
  input  in_2,
  input  [7:0] inB,
  output [7:0] aluOut
);

  wire [7:0] bit_extender_1_out;

  assign bit_extender_1_out = {{7{in_2}}, in_2};  // Bit_Extender bit_extender_1
  assign aluOut = inA & bit_extender_1_out & inB;  // AND_Gate and_1, 8 bits wide
endmodule

module inAorinB (
  input  [7:0] in_1,
  input  [7:0] in_2,
  input  in_3,
  output [7:0] out_4
);

  wire [7:0] bit_extender_1_out, or_1_out;

  assign bit_extender_1_out = {{7{in_3}}, in_3};  // Bit_Extender bit_extender_1
  assign or_1_out = in_1 | in_2;  // OR_Gate or_1, 8 bits wide
  assign out_4 = bit_extender_1_out & or_1_out;  // AND_Gate and_1, 8 bits wide
endmodule
